# Fritzing sketch Auto hand sanitizer (saved by Fritzing 0.9.3b)
breadboards: 1

parts:
  부품1 = Arduino Uno (Rev3)
  J1 = Piezo Speaker
  HC-SR04_Sensor_1 = HC-SR04 Ultrasonic Distance Sensor
  VCC3 = Battery block 9V  # not connected
  J2 = Basic Servo

nets:
  N1: 부품1.D9_PWM, J2.gnd
  N2: 부품1.D11_PWM/MOSI, J1.pin2
  GND: 부품1.GND, J1.pin1, HC-SR04_Sensor_1.GND, J2.pulse
  N3: 부품1.D2, HC-SR04_Sensor_1.TRIG
  N4: 부품1.D3_PWM, HC-SR04_Sensor_1.ECHO
  5V: 부품1.5V, HC-SR04_Sensor_1.VCC
  VIN: 부품1.VIN, J2.vcc
